# Fritzing sketch breadboard (saved by Fritzing 1.0.3b)
breadboards: 1

parts:
  SdModule1 = SdModule
  LCD1 = LCD screen
  R1 = Resistor [tolerance=±5% power=0.25W resistance=220 package=THT]
  Part1 = Arduino Nano (Rev3.0)

nets:
  GND: SdModule1.GND, LCD1.VSS, LCD1.V0, LCD1.R/W, LCD1.LED-, Part1.GND
  N1: SdModule1.SCK, Part1.D13/SCK
  N2: SdModule1.SS, Part1.D10
  5V: SdModule1.5V, LCD1.VDD, R1.Pin_0, Part1.5V
  N3: SdModule1.MISO, Part1.D12/MISO
  N4: SdModule1.MOSI, Part1.D11/MOSI
  N5: LCD1.RS, Part1.D7
  N6: LCD1.E, Part1.D8
  N7: LCD1.DB4, Part1.D2
  N8: LCD1.DB5, Part1.D3
  N9: LCD1.DB6, Part1.D4
  N10: LCD1.DB7, Part1.D5
  N11: LCD1.LED+, R1.Pin_1
